// Logisim project flipflop.circ as structural Verilog
module d_flip_flop (
  input  data,
  input  write,
  output memory
);

  wire and_1_out, and_2_out, nor_2_out, not_1_out;

  not not_1 (not_1_out, data);
  and and_1 (and_1_out, not_1_out, write);
  and and_2 (and_2_out, write, data);
  nor nor_1 (memory, and_1_out, nor_2_out);
  nor nor_2 (nor_2_out, memory, and_2_out);
endmodule

module guarded_d_flip_flop (
  input  data,
  input  write,
  output memory
);

  wire d_flip_flop_1_memory, not_1_out;

  not not_1 (not_1_out, write);
  d_flip_flop d_flip_flop_1 (.data(data), .write(write), .memory(d_flip_flop_1_memory));
  d_flip_flop d_flip_flop_2 (.data(d_flip_flop_1_memory), .write(not_1_out), .memory(memory));
endmodule

module d_flip_flop_8 (
  input  [7:0] data,
  input  write,
  output [7:0] Output_bus_1
);

  d_flip_flop d_flip_flop_1 (.data(data[0]), .write(write), .memory(Output_bus_1[0]));
  d_flip_flop d_flip_flop_2 (.data(data[1]), .write(write), .memory(Output_bus_1[1]));
  d_flip_flop d_flip_flop_3 (.data(data[2]), .write(write), .memory(Output_bus_1[2]));
  d_flip_flop d_flip_flop_4 (.data(data[3]), .write(write), .memory(Output_bus_1[3]));
  d_flip_flop d_flip_flop_5 (.data(data[4]), .write(write), .memory(Output_bus_1[4]));
  d_flip_flop d_flip_flop_6 (.data(data[5]), .write(write), .memory(Output_bus_1[5]));
  d_flip_flop d_flip_flop_7 (.data(data[6]), .write(write), .memory(Output_bus_1[6]));
  d_flip_flop d_flip_flop_8 (.data(data[7]), .write(write), .memory(Output_bus_1[7]));
endmodule

module word (
  input  [31:0] data_in,
  input  write,
  output [31:0] data_out
);

  wire clock_1_out;

  Register #(.trigger("high"), .width(32)) register_1 (
    .D(data_in), .en(write), .clk(clock_1_out), .Q(data_out));  // open: clr
  Clock clock_1 (.out(clock_1_out));
endmodule

module guarded_register (
  input  [31:0] data_in,
  input  write,
  output [31:0] data_out
);

  wire not_1_out;
  wire [31:0] word_1_data_out;

  not not_1 (not_1_out, write);
  word word_1 (.data_in(data_in), .write(write), .data_out(word_1_data_out));
  word word_2 (.data_in(word_1_data_out), .write(not_1_out), .data_out(data_out));
endmodule

module one_hot (
  input  index,
  input  data,
  output out0,
  output out1
);

  wire not_1_out;

  not not_1 (not_1_out, index);
  and and_1 (out0, not_1_out, data);
  and and_2 (out1, index, data);
endmodule

module one_hot_4 (
  input  [1:0] index,
  input  data,
  output [3:0] encoding
);

  wire one_hot_2_out0, one_hot_2_out1;

  one_hot one_hot_2 (.index(index[1]), .data(data), .out0(one_hot_2_out0), .out1(one_hot_2_out1));
  one_hot one_hot_1 (.index(index[0]), .data(one_hot_2_out0), .out0(encoding[0]), .out1(encoding[1]));
  one_hot one_hot_3 (.index(index[0]), .data(one_hot_2_out1), .out0(encoding[2]), .out1(encoding[3]));
endmodule

module one_hot_8 (
  input  [2:0] index,
  input  data,
  output [7:0] encoding
);

  wire one_hot_1_out0, one_hot_1_out1;

  one_hot one_hot_1 (.index(index[2]), .data(data), .out0(one_hot_1_out0), .out1(one_hot_1_out1));
  one_hot_4 one_hot_4_1 (.index(index[1:0]), .data(one_hot_1_out0), .encoding(encoding[3:0]));
  one_hot_4 one_hot_4_2 (.index(index[1:0]), .data(one_hot_1_out1), .encoding(encoding[7:4]));
endmodule

module one_hot_16 (
  input  [3:0] index,
  input  data,
  output [15:0] encoding
);

  wire [3:0] one_hot_4_5_encoding;

  one_hot_4 one_hot_4_5 (.index(index[3:2]), .data(data), .encoding(one_hot_4_5_encoding));
  one_hot_4 one_hot_4_1 (.index(index[1:0]), .data(one_hot_4_5_encoding[0]), .encoding(encoding[3:0]));
  one_hot_4 one_hot_4_2 (.index(index[1:0]), .data(one_hot_4_5_encoding[1]), .encoding(encoding[7:4]));
  one_hot_4 one_hot_4_3 (.index(index[1:0]), .data(one_hot_4_5_encoding[2]), .encoding(encoding[11:8]));
  one_hot_4 one_hot_4_4 (.index(index[1:0]), .data(one_hot_4_5_encoding[3]), .encoding(encoding[15:12]));
endmodule

module one_hot_32 (
  input  [4:0] index,
  input  data,
  output [31:0] encoding
);

  Demultiplexer #(.select(5)) demultiplexer_1 (
    .out0(encoding[0]), .out1(encoding[1]), .out2(encoding[2]), .out3(encoding[3]), .out4(encoding[4]),
    .out5(encoding[5]), .out6(encoding[6]), .out7(encoding[7]), .out8(encoding[8]), .out9(encoding[9]),
    .out10(encoding[10]), .out11(encoding[11]), .out12(encoding[12]), .out13(encoding[13]),
    .out14(encoding[14]), .out15(encoding[15]), .out16(encoding[16]), .out17(encoding[17]),
    .out18(encoding[18]), .out19(encoding[19]), .out20(encoding[20]), .out21(encoding[21]),
    .out22(encoding[22]), .out23(encoding[23]), .out24(encoding[24]), .out25(encoding[25]),
    .out26(encoding[26]), .out27(encoding[27]), .out28(encoding[28]), .out29(encoding[29]),
    .out30(encoding[30]), .out31(encoding[31]), .in(data), .sel(index));
endmodule

module mux (
  input  index,
  input  arg0,
  input  arg1,
  output mux_out
);

  wire and_1_out, and_2_out, not_1_out;

  not not_1 (not_1_out, index);
  and and_1 (and_1_out, not_1_out, arg0);
  and and_2 (and_2_out, index, arg1);
  or or_1 (mux_out, and_1_out, and_2_out);
endmodule

module mux_2x2 (
  input  index,
  input  [1:0] arg0,
  input  [1:0] arg1,
  output [1:0] mux_out
);

  mux mux_1 (.index(index), .arg0(arg0[0]), .arg1(arg1[0]), .mux_out(mux_out[0]));
  mux mux_2 (.index(index), .arg0(arg0[1]), .arg1(arg1[1]), .mux_out(mux_out[1]));
endmodule

module mux_2x4 (
  input  index,
  input  [3:0] arg0,
  input  [3:0] arg1,
  output [3:0] mux_out
);

  mux_2x2 mux_2x2_1 (.index(index), .arg0(arg0[1:0]), .arg1(arg1[1:0]), .mux_out(mux_out[1:0]));
  mux_2x2 mux_2x2_2 (.index(index), .arg0(arg0[3:2]), .arg1(arg1[3:2]), .mux_out(mux_out[3:2]));
endmodule

module mux_2x5 (
  input  index,
  input  [4:0] arg0,
  input  [4:0] arg1,
  output [4:0] mux_out
);

  Multiplexer #(.width(5)) multiplexer_1 (.in0(arg0), .in1(arg1), .out(mux_out), .sel(index));
endmodule

module mux_2x8 (
  input  index,
  input  [7:0] arg0,
  input  [7:0] arg1,
  output [7:0] mux_out
);

  mux_2x4 mux_2x4_1 (.index(index), .arg0(arg0[3:0]), .arg1(arg1[3:0]), .mux_out(mux_out[3:0]));
  mux_2x4 mux_2x4_2 (.index(index), .arg0(arg0[7:4]), .arg1(arg1[7:4]), .mux_out(mux_out[7:4]));
endmodule

module mux_2x16 (
  input  index,
  input  [15:0] arg0,
  input  [15:0] arg1,
  output [15:0] mux_out
);

  mux_2x8 mux_2x8_1 (.index(index), .arg0(arg0[7:0]), .arg1(arg1[7:0]), .mux_out(mux_out[7:0]));
  mux_2x8 mux_2x8_2 (.index(index), .arg0(arg0[15:8]), .arg1(arg1[15:8]), .mux_out(mux_out[15:8]));
endmodule

module mux_2x32 (
  input  index,
  input  [31:0] arg0,
  input  [31:0] arg1,
  output [31:0] mux_out
);

  Multiplexer #(.width(32)) multiplexer_1 (.in0(arg0), .in1(arg1), .out(mux_out), .sel(index));
endmodule

module mux_4x1 (
  input  [1:0] index,
  input  arg0,
  input  arg1,
  input  arg2,
  input  arg3,
  output mux_out
);

  wire mux_2_mux_out, mux_3_mux_out;

  mux mux_2 (.index(index[0]), .arg0(arg0), .arg1(arg1), .mux_out(mux_2_mux_out));
  mux mux_3 (.index(index[0]), .arg0(arg2), .arg1(arg3), .mux_out(mux_3_mux_out));
  mux mux_1 (.index(index[1]), .arg0(mux_2_mux_out), .arg1(mux_3_mux_out), .mux_out(mux_out));
endmodule

module mux_4x2 (
  input  [1:0] index,
  input  [1:0] arg0,
  input  [1:0] arg1,
  input  [1:0] arg2,
  input  [1:0] arg3,
  output [1:0] mux_out
);

  mux_4x1 mux_4x1_1 (
    .index(index), .arg0(arg0[0]), .arg1(arg1[0]), .arg2(arg2[0]), .arg3(arg3[0]), .mux_out(mux_out[0]));
  mux_4x1 mux_4x1_2 (
    .index(index), .arg0(arg0[1]), .arg1(arg1[1]), .arg2(arg2[1]), .arg3(arg3[1]), .mux_out(mux_out[1]));
endmodule

module mux_4x4 (
  input  [1:0] index,
  input  [3:0] arg0,
  input  [3:0] arg1,
  input  [3:0] arg2,
  input  [3:0] arg3,
  output [3:0] mux_out
);

  mux_4x2 mux_4x2_1 (
    .index(index), .arg0(arg0[1:0]), .arg1(arg1[1:0]), .arg2(arg2[1:0]), .arg3(arg3[1:0]),
    .mux_out(mux_out[1:0]));
  mux_4x2 mux_4x2_2 (
    .index(index), .arg0(arg0[3:2]), .arg1(arg1[3:2]), .arg2(arg2[3:2]), .arg3(arg3[3:2]),
    .mux_out(mux_out[3:2]));
endmodule

module mux_4x8 (
  input  [1:0] index,
  input  [7:0] arg0,
  input  [7:0] arg1,
  input  [7:0] arg2,
  input  [7:0] arg3,
  output [7:0] mux_out
);

  wire [7:0] mux_2x8_2_mux_out, mux_2x8_3_mux_out;

  mux_2x8 mux_2x8_2 (.index(index[0]), .arg0(arg0), .arg1(arg1), .mux_out(mux_2x8_2_mux_out));
  mux_2x8 mux_2x8_3 (.index(index[0]), .arg0(arg2), .arg1(arg3), .mux_out(mux_2x8_3_mux_out));
  mux_2x8 mux_2x8_1 (.index(index[1]), .arg0(mux_2x8_2_mux_out), .arg1(mux_2x8_3_mux_out), .mux_out(mux_out));
endmodule

module mux_4x32 (
  input  [1:0] index,
  input  [31:0] arg0,
  input  [31:0] arg1,
  input  [31:0] arg2,
  input  [31:0] arg3,
  output [31:0] mux_out
);

  Multiplexer #(.select(2), .width(32)) multiplexer_1 (
    .in0(arg0), .in1(arg1), .in2(arg2), .in3(arg3), .out(mux_out), .sel(index));
endmodule

module mux_8x32 (
  input  [2:0] index,
  input  [31:0] arg0,
  input  [31:0] arg1,
  input  [31:0] arg2,
  input  [31:0] arg3,
  input  [31:0] arg4,
  input  [31:0] arg5,
  input  [31:0] arg6,
  input  [31:0] arg7,
  output [31:0] mux_out
);

  Multiplexer #(.select(3), .width(32)) multiplexer_1 (
    .in0(arg0), .in1(arg1), .in2(arg2), .in3(arg3), .in4(arg4), .in5(arg5), .in6(arg6), .in7(arg7),
    .out(mux_out), .sel(index));
endmodule

module mux_16x8 (
  input  [3:0] index,
  input  [7:0] arg0,
  input  [7:0] arg1,
  input  [7:0] arg2,
  input  [7:0] arg3,
  input  [7:0] arg4,
  input  [7:0] arg5,
  input  [7:0] arg6,
  input  [7:0] arg7,
  input  [7:0] arg8,
  input  [7:0] arg9,
  input  [7:0] arg10,
  input  [7:0] arg11,
  input  [7:0] arg12,
  input  [7:0] arg13,
  input  [7:0] arg14,
  input  [7:0] arg15,
  output [7:0] mux_out
);

  Multiplexer #(.select(4), .width(8)) multiplexer_1 (
    .in0(arg0), .in1(arg1), .in2(arg2), .in3(arg3), .in4(arg4), .in5(arg5), .in6(arg6), .in7(arg7),
    .in8(arg8), .in9(arg9), .in10(arg10), .in11(arg11), .in12(arg12), .in13(arg13), .in14(arg14),
    .in15(arg15), .out(mux_out), .sel(index));
endmodule

module mux_16x32 (
  input  [3:0] index,
  input  [31:0] arg0,
  input  [31:0] arg1,
  input  [31:0] arg2,
  input  [31:0] arg3,
  input  [31:0] arg4,
  input  [31:0] arg5,
  input  [31:0] arg6,
  input  [31:0] arg7,
  input  [31:0] arg8,
  input  [31:0] arg9,
  input  [31:0] arg10,
  input  [31:0] arg11,
  input  [31:0] arg12,
  input  [31:0] arg13,
  input  [31:0] arg14,
  input  [31:0] arg15,
  output [31:0] mux_out
);

  wire [31:0] mux_4x32_2_mux_out, mux_4x32_3_mux_out, mux_4x32_4_mux_out, mux_4x32_5_mux_out;

  mux_4x32 mux_4x32_2 (
    .index(index[1:0]), .arg0(arg0), .arg1(arg1), .arg2(arg2), .arg3(arg3), .mux_out(mux_4x32_2_mux_out));
  mux_4x32 mux_4x32_3 (
    .index(index[1:0]), .arg0(arg4), .arg1(arg5), .arg2(arg6), .arg3(arg7), .mux_out(mux_4x32_3_mux_out));
  mux_4x32 mux_4x32_4 (
    .index(index[1:0]), .arg0(arg8), .arg1(arg9), .arg2(arg10), .arg3(arg11), .mux_out(mux_4x32_4_mux_out));
  mux_4x32 mux_4x32_5 (
    .index(index[1:0]), .arg0(arg12), .arg1(arg13), .arg2(arg14), .arg3(arg15), .mux_out(mux_4x32_5_mux_out));
  mux_4x32 mux_4x32_1 (
    .index(index[3:2]), .arg0(mux_4x32_2_mux_out), .arg1(mux_4x32_3_mux_out), .arg2(mux_4x32_4_mux_out),
    .arg3(mux_4x32_5_mux_out), .mux_out(mux_out));
endmodule

module mux_32x32 (
  input  [4:0] index,
  input  [31:0] arg0,
  input  [31:0] arg1,
  input  [31:0] arg2,
  input  [31:0] arg3,
  input  [31:0] arg4,
  input  [31:0] arg5,
  input  [31:0] arg6,
  input  [31:0] arg7,
  input  [31:0] arg8,
  input  [31:0] arg9,
  input  [31:0] arg10,
  input  [31:0] arg11,
  input  [31:0] arg12,
  input  [31:0] arg13,
  input  [31:0] arg14,
  input  [31:0] arg15,
  input  [31:0] arg16,
  input  [31:0] arg17,
  input  [31:0] arg18,
  input  [31:0] arg19,
  input  [31:0] arg20,
  input  [31:0] arg21,
  input  [31:0] arg22,
  input  [31:0] arg23,
  input  [31:0] arg24,
  input  [31:0] arg25,
  input  [31:0] arg26,
  input  [31:0] arg27,
  input  [31:0] arg28,
  input  [31:0] arg29,
  input  [31:0] arg30,
  input  [31:0] arg31,
  output [31:0] mux_out
);

  Multiplexer #(.select(5), .width(32)) multiplexer_1 (
    .in0(arg0), .in1(arg1), .in2(arg2), .in3(arg3), .in4(arg4), .in5(arg5), .in6(arg6), .in7(arg7),
    .in8(arg8), .in9(arg9), .in10(arg10), .in11(arg11), .in12(arg12), .in13(arg13), .in14(arg14),
    .in15(arg15), .in16(arg16), .in17(arg17), .in18(arg18), .in19(arg19), .in20(arg20), .in21(arg21),
    .in22(arg22), .in23(arg23), .in24(arg24), .in25(arg25), .in26(arg26), .in27(arg27), .in28(arg28),
    .in29(arg29), .in30(arg30), .in31(arg31), .out(mux_out), .sel(index));
endmodule

module ram_chunk (
  input  [3:0] word_index,
  input  [31:0] data_in,
  input  write,
  output [31:0] data_out
);

  wire [15:0] one_hot_16_1_encoding;
  wire [31:0] word_1_data_out, word_2_data_out, word_3_data_out, word_4_data_out, word_5_data_out,
       word_6_data_out, word_7_data_out, word_8_data_out, word_9_data_out, word_10_data_out,
       word_11_data_out, word_12_data_out, word_13_data_out, word_14_data_out, word_15_data_out,
       word_16_data_out;

  one_hot_16 one_hot_16_1 (.index(word_index), .data(write), .encoding(one_hot_16_1_encoding));
  word word_1 (.data_in(data_in), .write(one_hot_16_1_encoding[0]), .data_out(word_1_data_out));
  word word_2 (.data_in(data_in), .write(one_hot_16_1_encoding[1]), .data_out(word_2_data_out));
  word word_3 (.data_in(data_in), .write(one_hot_16_1_encoding[2]), .data_out(word_3_data_out));
  word word_4 (.data_in(data_in), .write(one_hot_16_1_encoding[3]), .data_out(word_4_data_out));
  word word_5 (.data_in(data_in), .write(one_hot_16_1_encoding[4]), .data_out(word_5_data_out));
  word word_6 (.data_in(data_in), .write(one_hot_16_1_encoding[5]), .data_out(word_6_data_out));
  word word_7 (.data_in(data_in), .write(one_hot_16_1_encoding[6]), .data_out(word_7_data_out));
  word word_8 (.data_in(data_in), .write(one_hot_16_1_encoding[7]), .data_out(word_8_data_out));
  word word_9 (.data_in(data_in), .write(one_hot_16_1_encoding[8]), .data_out(word_9_data_out));
  word word_10 (.data_in(data_in), .write(one_hot_16_1_encoding[9]), .data_out(word_10_data_out));
  word word_11 (.data_in(data_in), .write(one_hot_16_1_encoding[10]), .data_out(word_11_data_out));
  word word_12 (.data_in(data_in), .write(one_hot_16_1_encoding[11]), .data_out(word_12_data_out));
  word word_13 (.data_in(data_in), .write(one_hot_16_1_encoding[12]), .data_out(word_13_data_out));
  word word_14 (.data_in(data_in), .write(one_hot_16_1_encoding[13]), .data_out(word_14_data_out));
  word word_15 (.data_in(data_in), .write(one_hot_16_1_encoding[14]), .data_out(word_15_data_out));
  word word_16 (.data_in(data_in), .write(one_hot_16_1_encoding[15]), .data_out(word_16_data_out));
  mux_16x32 mux_16x32_1 (
    .index(word_index), .arg0(word_1_data_out), .arg1(word_2_data_out), .arg2(word_3_data_out),
    .arg3(word_4_data_out), .arg4(word_5_data_out), .arg5(word_6_data_out), .arg6(word_7_data_out),
    .arg7(word_8_data_out), .arg8(word_9_data_out), .arg9(word_10_data_out), .arg10(word_11_data_out),
    .arg11(word_12_data_out), .arg12(word_13_data_out), .arg13(word_14_data_out), .arg14(word_15_data_out),
    .arg15(word_16_data_out), .mux_out(data_out));
endmodule

module ram_block (
  input  [7:0] word_index,
  input  [31:0] data_in,
  input  write,
  output [31:0] data_out
);

  wire [15:0] one_hot_16_1_encoding;
  wire [31:0] ram_chunk_1_data_out, ram_chunk_2_data_out, ram_chunk_3_data_out, ram_chunk_4_data_out,
       ram_chunk_5_data_out, ram_chunk_6_data_out, ram_chunk_7_data_out, ram_chunk_8_data_out,
       ram_chunk_9_data_out, ram_chunk_10_data_out, ram_chunk_11_data_out, ram_chunk_12_data_out,
       ram_chunk_13_data_out, ram_chunk_14_data_out, ram_chunk_15_data_out, ram_chunk_16_data_out;

  one_hot_16 one_hot_16_1 (.index(word_index[7:4]), .data(write), .encoding(one_hot_16_1_encoding));
  ram_chunk ram_chunk_1 (
    .word_index(word_index[3:0]), .data_in(data_in), .write(one_hot_16_1_encoding[0]),
    .data_out(ram_chunk_1_data_out));
  ram_chunk ram_chunk_2 (
    .word_index(word_index[3:0]), .data_in(data_in), .write(one_hot_16_1_encoding[1]),
    .data_out(ram_chunk_2_data_out));
  ram_chunk ram_chunk_3 (
    .word_index(word_index[3:0]), .data_in(data_in), .write(one_hot_16_1_encoding[2]),
    .data_out(ram_chunk_3_data_out));
  ram_chunk ram_chunk_4 (
    .word_index(word_index[3:0]), .data_in(data_in), .write(one_hot_16_1_encoding[3]),
    .data_out(ram_chunk_4_data_out));
  ram_chunk ram_chunk_5 (
    .word_index(word_index[3:0]), .data_in(data_in), .write(one_hot_16_1_encoding[4]),
    .data_out(ram_chunk_5_data_out));
  ram_chunk ram_chunk_6 (
    .word_index(word_index[3:0]), .data_in(data_in), .write(one_hot_16_1_encoding[5]),
    .data_out(ram_chunk_6_data_out));
  ram_chunk ram_chunk_7 (
    .word_index(word_index[3:0]), .data_in(data_in), .write(one_hot_16_1_encoding[6]),
    .data_out(ram_chunk_7_data_out));
  ram_chunk ram_chunk_8 (
    .word_index(word_index[3:0]), .data_in(data_in), .write(one_hot_16_1_encoding[7]),
    .data_out(ram_chunk_8_data_out));
  ram_chunk ram_chunk_9 (
    .word_index(word_index[3:0]), .data_in(data_in), .write(one_hot_16_1_encoding[8]),
    .data_out(ram_chunk_9_data_out));
  ram_chunk ram_chunk_10 (
    .word_index(word_index[3:0]), .data_in(data_in), .write(one_hot_16_1_encoding[9]),
    .data_out(ram_chunk_10_data_out));
  ram_chunk ram_chunk_11 (
    .word_index(word_index[3:0]), .data_in(data_in), .write(one_hot_16_1_encoding[10]),
    .data_out(ram_chunk_11_data_out));
  ram_chunk ram_chunk_12 (
    .word_index(word_index[3:0]), .data_in(data_in), .write(one_hot_16_1_encoding[11]),
    .data_out(ram_chunk_12_data_out));
  ram_chunk ram_chunk_13 (
    .word_index(word_index[3:0]), .data_in(data_in), .write(one_hot_16_1_encoding[12]),
    .data_out(ram_chunk_13_data_out));
  ram_chunk ram_chunk_14 (
    .word_index(word_index[3:0]), .data_in(data_in), .write(one_hot_16_1_encoding[13]),
    .data_out(ram_chunk_14_data_out));
  ram_chunk ram_chunk_15 (
    .word_index(word_index[3:0]), .data_in(data_in), .write(one_hot_16_1_encoding[14]),
    .data_out(ram_chunk_15_data_out));
  ram_chunk ram_chunk_16 (
    .word_index(word_index[3:0]), .data_in(data_in), .write(one_hot_16_1_encoding[15]),
    .data_out(ram_chunk_16_data_out));
  mux_16x32 mux_16x32_1 (
    .index(word_index[7:4]), .arg0(ram_chunk_1_data_out), .arg1(ram_chunk_2_data_out),
    .arg2(ram_chunk_3_data_out), .arg3(ram_chunk_4_data_out), .arg4(ram_chunk_5_data_out),
    .arg5(ram_chunk_6_data_out), .arg6(ram_chunk_7_data_out), .arg7(ram_chunk_8_data_out),
    .arg8(ram_chunk_9_data_out), .arg9(ram_chunk_10_data_out), .arg10(ram_chunk_11_data_out),
    .arg11(ram_chunk_12_data_out), .arg12(ram_chunk_13_data_out), .arg13(ram_chunk_14_data_out),
    .arg14(ram_chunk_15_data_out), .arg15(ram_chunk_16_data_out), .mux_out(data_out));
endmodule

module ram_adapter (
  input  [5:0] word_index,
  input  [31:0] data_in,
  input  write,
  output [31:0] data_out
);

  wire clock_1_out;

  Clock clock_1 (.out(clock_1_out));
  RAM #(.addrWidth(6), .asyncread("true"), .dataWidth(32)) RAM_1 (
    .addr(word_index), .we(write), .oe(1'b1), .clk(clock_1_out), .din(data_in), .dout(data_out));
endmodule

module ram_module (
  input  [31:0] pointer,
  input  [31:0] data_in,
  input  write,
  output [31:0] word,
  output [15:0] halfword,
  output [7:0] \byte 
);

  ram_adapter ram_adapter_1 (.word_index(pointer[7:2]), .data_in(data_in), .write(write), .data_out(word));
  mux_2x16 mux_2x16_1 (.index(pointer[1]), .arg0(word[15:0]), .arg1(word[31:16]), .mux_out(halfword));
  mux_4x8 mux_4x8_1 (
    .index(pointer[1:0]), .arg0(word[7:0]), .arg1(word[15:8]), .arg2(word[23:16]), .arg3(word[31:24]),
    .mux_out(\byte ));
endmodule

module register_module (
  input  [4:0] rs1,
  input  [4:0] rs2,
  input  [4:0] rd,
  input  [31:0] data_in,
  input  write,
  output [31:0] rs1_val,
  output [31:0] rs2_val,
  output [31:0] a0_val
);

  wire read;
  wire [31:0] mux_32x32_1_mux_out, mux_32x32_2_mux_out, one_hot_32_1_encoding, x1, x2, x3, x4, x5, x6, x7,
       x8, x9, x11, x12, x13, x14, x15, x16, x17, x18, x19, x20, x21, x22, x23, x24, x25, x26, x27, x28, x29,
       x30, x31;

  not not_1 (read, write);
  one_hot_32 one_hot_32_1 (.index(rd), .data(write), .encoding(one_hot_32_1_encoding));
  // NoConnect on one_hot_32_1_encoding[0]
  word word_2 (.data_in(data_in), .write(one_hot_32_1_encoding[1]), .data_out(x1));
  word word_3 (.data_in(data_in), .write(one_hot_32_1_encoding[2]), .data_out(x2));
  word word_4 (.data_in(data_in), .write(one_hot_32_1_encoding[3]), .data_out(x3));
  word word_5 (.data_in(data_in), .write(one_hot_32_1_encoding[4]), .data_out(x4));
  word word_6 (.data_in(data_in), .write(one_hot_32_1_encoding[5]), .data_out(x5));
  word word_7 (.data_in(data_in), .write(one_hot_32_1_encoding[6]), .data_out(x6));
  word word_9 (.data_in(data_in), .write(one_hot_32_1_encoding[7]), .data_out(x7));
  word word_10 (.data_in(data_in), .write(one_hot_32_1_encoding[8]), .data_out(x8));
  word word_11 (.data_in(data_in), .write(one_hot_32_1_encoding[9]), .data_out(x9));
  word word_12 (.data_in(data_in), .write(one_hot_32_1_encoding[10]), .data_out(a0_val));
  word word_13 (.data_in(data_in), .write(one_hot_32_1_encoding[11]), .data_out(x11));
  word word_14 (.data_in(data_in), .write(one_hot_32_1_encoding[12]), .data_out(x12));
  word word_15 (.data_in(data_in), .write(one_hot_32_1_encoding[13]), .data_out(x13));
  word word_16 (.data_in(data_in), .write(one_hot_32_1_encoding[14]), .data_out(x14));
  word word_17 (.data_in(data_in), .write(one_hot_32_1_encoding[15]), .data_out(x15));
  word word_18 (.data_in(data_in), .write(one_hot_32_1_encoding[16]), .data_out(x16));
  word word_19 (.data_in(data_in), .write(one_hot_32_1_encoding[17]), .data_out(x17));
  word word_20 (.data_in(data_in), .write(one_hot_32_1_encoding[18]), .data_out(x18));
  word word_21 (.data_in(data_in), .write(one_hot_32_1_encoding[19]), .data_out(x19));
  word word_22 (.data_in(data_in), .write(one_hot_32_1_encoding[20]), .data_out(x20));
  word word_23 (.data_in(data_in), .write(one_hot_32_1_encoding[21]), .data_out(x21));
  word word_24 (.data_in(data_in), .write(one_hot_32_1_encoding[22]), .data_out(x22));
  word word_25 (.data_in(data_in), .write(one_hot_32_1_encoding[23]), .data_out(x23));
  word word_26 (.data_in(data_in), .write(one_hot_32_1_encoding[24]), .data_out(x24));
  word word_27 (.data_in(data_in), .write(one_hot_32_1_encoding[25]), .data_out(x25));
  word word_28 (.data_in(data_in), .write(one_hot_32_1_encoding[26]), .data_out(x26));
  word word_29 (.data_in(data_in), .write(one_hot_32_1_encoding[27]), .data_out(x27));
  word word_30 (.data_in(data_in), .write(one_hot_32_1_encoding[28]), .data_out(x28));
  word word_31 (.data_in(data_in), .write(one_hot_32_1_encoding[29]), .data_out(x29));
  word word_32 (.data_in(data_in), .write(one_hot_32_1_encoding[30]), .data_out(x30));
  word word_33 (.data_in(data_in), .write(one_hot_32_1_encoding[31]), .data_out(x31));
  mux_32x32 mux_32x32_1 (
    .index(rs1), .arg0({32{1'b0}}), .arg1(x1), .arg2(x2), .arg3(x3), .arg4(x4), .arg5(x5), .arg6(x6),
    .arg7(x7), .arg8(x8), .arg9(x9), .arg10(a0_val), .arg11(x11), .arg12(x12), .arg13(x13), .arg14(x14),
    .arg15(x15), .arg16(x16), .arg17(x17), .arg18(x18), .arg19(x19), .arg20(x20), .arg21(x21), .arg22(x22),
    .arg23(x23), .arg24(x24), .arg25(x25), .arg26(x26), .arg27(x27), .arg28(x28), .arg29(x29), .arg30(x30),
    .arg31(x31), .mux_out(mux_32x32_1_mux_out));
  mux_32x32 mux_32x32_2 (
    .index(rs2), .arg0({32{1'b0}}), .arg1(x1), .arg2(x2), .arg3(x3), .arg4(x4), .arg5(x5), .arg6(x6),
    .arg7(x7), .arg8(x8), .arg9(x9), .arg10(a0_val), .arg11(x11), .arg12(x12), .arg13(x13), .arg14(x14),
    .arg15(x15), .arg16(x16), .arg17(x17), .arg18(x18), .arg19(x19), .arg20(x20), .arg21(x21), .arg22(x22),
    .arg23(x23), .arg24(x24), .arg25(x25), .arg26(x26), .arg27(x27), .arg28(x28), .arg29(x29), .arg30(x30),
    .arg31(x31), .mux_out(mux_32x32_2_mux_out));
  word word_1 (.data_in(mux_32x32_1_mux_out), .write(read), .data_out(rs1_val));
  word word_8 (.data_in(mux_32x32_2_mux_out), .write(read), .data_out(rs2_val));

  // Other names for the same wires on the sheet: x10[31:0] = a0_val
endmodule

module adder_1 (
  input  carry_in,
  input  A,
  input  B,
  output sum,
  output carry_out
);

  wire and_1_out, and_2_out, and_3_out, xor_1_out;

  and and_1 (and_1_out, carry_in, A);
  xor xor_1 (xor_1_out, A, B);
  and and_2 (and_2_out, B, A);
  and and_3 (and_3_out, carry_in, B);
  xor xor_2 (sum, carry_in, xor_1_out);
  or or_1 (carry_out, and_2_out, and_3_out, and_1_out);
endmodule

module adder_2 (
  input  carry_in,
  input  [1:0] A,
  input  [1:0] B,
  output [1:0] sum,
  output carry_out
);

  wire adder_1_1_carry_out;

  adder_1 adder_1_1 (.carry_in(carry_in), .A(A[0]), .B(B[0]), .sum(sum[0]), .carry_out(adder_1_1_carry_out));
  adder_1 adder_1_2 (.carry_in(adder_1_1_carry_out), .A(A[1]), .B(B[1]), .sum(sum[1]), .carry_out(carry_out));
endmodule

module adder_4 (
  input  carry_in,
  input  [3:0] A,
  input  [3:0] B,
  output [3:0] sum,
  output carry_out
);

  wire adder_2_1_carry_out;

  adder_2 adder_2_1 (.carry_in(carry_in), .A(A[1:0]), .B(B[1:0]), .sum(sum[1:0]), .carry_out(adder_2_1_carry_out));
  adder_2 adder_2_2 (.carry_in(adder_2_1_carry_out), .A(A[3:2]), .B(B[3:2]), .sum(sum[3:2]), .carry_out(carry_out));
endmodule

module adder_8 (
  input  carry_in,
  input  [7:0] A,
  input  [7:0] B,
  output [7:0] sum,
  output carry_out
);

  wire adder_4_1_carry_out;

  adder_4 adder_4_1 (.carry_in(carry_in), .A(A[3:0]), .B(B[3:0]), .sum(sum[3:0]), .carry_out(adder_4_1_carry_out));
  adder_4 adder_4_2 (.carry_in(adder_4_1_carry_out), .A(A[7:4]), .B(B[7:4]), .sum(sum[7:4]), .carry_out(carry_out));
endmodule

module adder_16 (
  input  carry_in,
  input  [15:0] A,
  input  [15:0] B,
  output [15:0] sum,
  output carry_out
);

  wire adder_8_1_carry_out;

  adder_8 adder_8_1 (.carry_in(carry_in), .A(A[7:0]), .B(B[7:0]), .sum(sum[7:0]), .carry_out(adder_8_1_carry_out));
  adder_8 adder_8_2 (.carry_in(adder_8_1_carry_out), .A(A[15:8]), .B(B[15:8]), .sum(sum[15:8]), .carry_out(carry_out));
endmodule

module adder_32 (
  input  carry_in,
  input  [31:0] A,
  input  [31:0] B,
  output [31:0] sum,
  output carry_out
);

  wire adder_16_1_carry_out;

  adder_16 adder_16_1 (
    .carry_in(carry_in), .A(A[15:0]), .B(B[15:0]), .sum(sum[15:0]), .carry_out(adder_16_1_carry_out));
  adder_16 adder_16_2 (
    .carry_in(adder_16_1_carry_out), .A(A[31:16]), .B(B[31:16]), .sum(sum[31:16]), .carry_out(carry_out));
endmodule

module nc_adder_32 (
  input  [31:0] A,
  input  [31:0] B,
  output [31:0] sum
);

  wire adder_32_1_carry_out;

  adder_32 adder_32_1 (.carry_in(1'b0), .A(A), .B(B), .sum(sum), .carry_out(adder_32_1_carry_out));
  // NoConnect on adder_32_1_carry_out
endmodule

module cmp_7 (
  input  [6:0] A,
  input  [6:0] B,
  output equal
);

  wire [6:0] xor_1_out;

  assign xor_1_out = A ^ B;  // XOR_Gate xor_1, 7 bits wide
  nor nor_1 (equal, xor_1_out[0], xor_1_out[1], xor_1_out[2], xor_1_out[3], xor_1_out[4], xor_1_out[5], xor_1_out[6]);
endmodule

module cmp_3 (
  input  [2:0] A,
  input  [2:0] B,
  output equal
);

  wire [2:0] xor_1_out;

  nor nor_1 (equal, xor_1_out[0], xor_1_out[1], xor_1_out[2]);
  assign xor_1_out = A ^ B;  // XOR_Gate xor_1, 3 bits wide
endmodule

module comparator_32 (
  input  [31:0] A,
  input  [31:0] B,
  output eq,
  output lts,
  output gts,
  output ltu,
  output gtu
);

  wire adder_32_1_carry_out, xor_1_out;
  wire [31:0] adder_32_1_sum, not_1_out;

  assign not_1_out = ~B;  // NOT_Gate not_1, 32 bits wide
  xor xor_1 (xor_1_out, A[31], B[31]);
  adder_32 adder_32_1 (.carry_in(1'b1), .A(A), .B(not_1_out), .sum(adder_32_1_sum), .carry_out(adder_32_1_carry_out));
  nor nor_1 (eq, adder_32_1_sum[15], adder_32_1_sum[0], adder_32_1_sum[1], adder_32_1_sum[2], adder_32_1_sum[3], adder_32_1_sum[4], adder_32_1_sum[5], adder_32_1_sum[7], adder_32_1_sum[8], adder_32_1_sum[9], adder_32_1_sum[10], adder_32_1_sum[11], adder_32_1_sum[12], adder_32_1_sum[13], adder_32_1_sum[14], adder_32_1_sum[16], adder_32_1_sum[17], adder_32_1_sum[18], adder_32_1_sum[19], adder_32_1_sum[20], adder_32_1_sum[21], adder_32_1_sum[22], adder_32_1_sum[23], adder_32_1_sum[24], adder_32_1_sum[25], adder_32_1_sum[26], adder_32_1_sum[27], adder_32_1_sum[28], adder_32_1_sum[29], adder_32_1_sum[30], adder_32_1_sum[31]);
  not not_2 (ltu, adder_32_1_carry_out);
  and and_1 (gtu, ~eq, adder_32_1_carry_out);  // AND_Gate
  mux mux_1 (.index(xor_1_out), .arg0(adder_32_1_sum[31]), .arg1(A[31]), .mux_out(lts));
  nor nor_2 (gts, eq, lts);
endmodule

module lshift (
  input  [31:0] val,
  input  [4:0] shamt,
  output [31:0] shifted
);

  wire [31:0] mux_2x32_1_mux_out, mux_2x32_2_mux_out, mux_2x32_3_mux_out, mux_2x32_4_mux_out;

  mux_2x32 mux_2x32_1 (.index(shamt[4]), .arg0(val), .arg1({val[15:0], {16{1'b0}}}), .mux_out(mux_2x32_1_mux_out));
  mux_2x32 mux_2x32_2 (
    .index(shamt[3]), .arg0(mux_2x32_1_mux_out), .arg1({mux_2x32_1_mux_out[23:0], {8{1'b0}}}),
    .mux_out(mux_2x32_2_mux_out));
  mux_2x32 mux_2x32_3 (
    .index(shamt[2]), .arg0(mux_2x32_2_mux_out), .arg1({mux_2x32_2_mux_out[27:0], 4'b0000}),
    .mux_out(mux_2x32_3_mux_out));
  mux_2x32 mux_2x32_4 (
    .index(shamt[1]), .arg0(mux_2x32_3_mux_out), .arg1({mux_2x32_3_mux_out[29:0], 2'b00}),
    .mux_out(mux_2x32_4_mux_out));
  mux_2x32 mux_2x32_5 (
    .index(shamt[0]), .arg0(mux_2x32_4_mux_out), .arg1({mux_2x32_4_mux_out[30:0], 1'b0}), .mux_out(shifted));
endmodule

module rshift (
  input  [31:0] val,
  input  [4:0] shamt,
  input  arith,
  output [31:0] shifted
);

  wire and_1_out;
  wire [31:0] bit_extender_1_out, bit_extender_2_out, bit_extender_3_out, bit_extender_4_out,
       bit_extender_5_out, mux_2x32_1_mux_out, mux_2x32_2_mux_out, mux_2x32_3_mux_out, mux_2x32_4_mux_out;

  and and_1 (and_1_out, arith, val[31]);
  assign bit_extender_1_out = {{16{and_1_out}}, val[31:16]};  // Bit_Extender bit_extender_1
  mux_2x32 mux_2x32_1 (.index(shamt[4]), .arg0(val), .arg1(bit_extender_1_out), .mux_out(mux_2x32_1_mux_out));
  assign bit_extender_2_out = {{8{and_1_out}}, mux_2x32_1_mux_out[31:8]};  // Bit_Extender bit_extender_2
  mux_2x32 mux_2x32_2 (
    .index(shamt[3]), .arg0(mux_2x32_1_mux_out), .arg1(bit_extender_2_out), .mux_out(mux_2x32_2_mux_out));
  assign bit_extender_3_out = {{4{and_1_out}}, mux_2x32_2_mux_out[31:4]};  // Bit_Extender bit_extender_3
  mux_2x32 mux_2x32_3 (
    .index(shamt[2]), .arg0(mux_2x32_2_mux_out), .arg1(bit_extender_3_out), .mux_out(mux_2x32_3_mux_out));
  assign bit_extender_4_out = {{2{and_1_out}}, mux_2x32_3_mux_out[31:2]};  // Bit_Extender bit_extender_4
  mux_2x32 mux_2x32_4 (
    .index(shamt[1]), .arg0(mux_2x32_3_mux_out), .arg1(bit_extender_4_out), .mux_out(mux_2x32_4_mux_out));
  assign bit_extender_5_out = {{1{and_1_out}}, mux_2x32_4_mux_out[31:1]};  // Bit_Extender bit_extender_5
  mux_2x32 mux_2x32_5 (.index(shamt[0]), .arg0(mux_2x32_4_mux_out), .arg1(bit_extender_5_out), .mux_out(shifted));
endmodule

module counter_3 (
  input  reset,
  input  clock,
  output s0,
  output s1,
  output s2
);

  wire and_1_out, and_2_out, guarded_d_flip_flop_1_memory, guarded_d_flip_flop_2_memory,
       guarded_d_flip_flop_3_memory, or_1_out, or_2_out;

  or or_1 (or_1_out, reset, clock);
  or or_2 (or_2_out, guarded_d_flip_flop_3_memory, reset);
  and and_1 (and_1_out, guarded_d_flip_flop_1_memory, ~reset);  // AND_Gate
  and and_2 (and_2_out, guarded_d_flip_flop_2_memory, ~reset);  // AND_Gate
  guarded_d_flip_flop guarded_d_flip_flop_1 (.data(or_2_out), .write(or_1_out), .memory(guarded_d_flip_flop_1_memory));
  guarded_d_flip_flop guarded_d_flip_flop_2 (.data(and_1_out), .write(or_1_out), .memory(guarded_d_flip_flop_2_memory));
  guarded_d_flip_flop guarded_d_flip_flop_3 (.data(and_2_out), .write(or_1_out), .memory(guarded_d_flip_flop_3_memory));
  and and_3 (s0, guarded_d_flip_flop_1_memory, clock);
  and and_4 (s1, guarded_d_flip_flop_2_memory, clock);
  and and_5 (s2, guarded_d_flip_flop_3_memory, clock);
endmodule

module cpu (
  input  manual_exec,
  input  [31:0] manual_instr,
  input  manual_instr_write,
  input  [31:0] manual_pc,
  input  manual_pc_write,
  input  reset,
  input  clock,
  output [31:0] a0
);

  wire adder_32_1_carry_out, and_1_out, and_2_out, and_3_out, and_5_out, and_6_out, and_10_out, and_11_out,
       and_12_out, and_13_out, and_18_out, and_20_out, and_22_out, and_23_out, and_24_out,
       comparator_32_1_eq, comparator_32_1_lts, comparator_32_1_ltu, exec, instr_write, jump, load_store,
       mux_4x1_1_mux_out, nand_1_out, or_1_out, or_2_out, or_3_out, pc_write, reg_write, xor_3_out;
  wire [2:0] funct3;
  wire [4:0] i5, i12, mux_2x5_1_mux_out;
  wire [6:0] funct7, instr;
  wire [7:0] ram_byte;
  wire [7:3] i20;
  wire [15:0] ram_halfword;
  wire [31:0] A, adder_32_1_sum, alu_reg_data, and_7_out, and_8_out, and_9_out, B, bit_extender_3_out,
       bit_extender_4_out, bit_extender_5_out, bit_extender_6_out, bit_extender_7_out, bit_extender_8_out,
       bit_extender_9_out, bit_extender_10_out, bit_extender_11_out, bit_extender_12_out,
       bit_extender_13_out, bit_extender_14_out, i5_7_32, i12_32, instr_data, jump_reg_data, load_reg_data,
       load_store_pointer, lshift_1_shifted, lshift_2_shifted, lshift_3_shifted, lshift_4_shifted,
       lshift_5_shifted, mux_2x32_5_mux_out, mux_2x32_6_mux_out, mux_2x32_7_mux_out, mux_2x32_8_mux_out,
       mux_2x32_9_mux_out, mux_2x32_10_mux_out, mux_4x32_1_mux_out, mux_4x32_2_mux_out, mux_8x32_1_mux_out,
       nc_adder_32_2_sum, nc_adder_32_3_sum, nc_adder_32_4_sum, next_pc, or_4_out, or_5_out, or_6_out, pc,
       pc_data, pointer, ram_data, ram_word, reg_data, rs2v, rshift_1_shifted, ui_reg_data, xor_1_out,
       xor_2_out;

  or or_1 (or_1_out, exec, manual_exec);
  assign i12_32 = {{20{funct7[6]}}, {funct7, i12}};  // Bit_Extender bit_extender_1
  assign i5_7_32 = {{20{funct7[6]}}, {funct7, i5}};  // Bit_Extender bit_extender_2
  or or_2 (or_2_out, instr_write, manual_instr_write);
  or or_3 (or_3_out, pc_write, manual_pc_write);
  and and_1 (and_1_out, reg_write, or_1_out);
  and and_2 (and_2_out, instr[5], or_1_out);
  counter_3 counter_3_1 (.reset(reset), .clock(clock), .s0(instr_write), .s1(exec), .s2(pc_write));
  guarded_register instruction (
    .data_in(instr_data), .write(or_2_out), .data_out({funct7, i12, i20, funct3, i5, instr}));
  guarded_register program_counter (.data_in(pc_data), .write(or_3_out), .data_out(pc));
  register_module registers (
    .rs1(i20), .rs2(i12), .rd(i5), .data_in(reg_data), .write(and_1_out), .rs1_val(A), .rs2_val(rs2v),
    .a0_val(a0));
  ram_module ram (
    .pointer(pointer), .data_in(ram_data), .write(and_2_out), .word(ram_word), .halfword(ram_halfword),
    .\byte (ram_byte));
  // Probe on pc
  // Probe on {funct7, i12, i20, funct3, i5, instr}
  // Probe on i5
  // Probe on pointer
  // Probe on ram_word
  and and_3 (and_3_out, funct7[4], funct7[5], instr[5]);
  // Probe on i20
  // Probe on i12
  // Probe on A
  // Probe on rs2v
  assign bit_extender_3_out = {{31{and_3_out}}, and_3_out};  // Bit_Extender bit_extender_3
  mux_2x5 mux_2x5_1 (.index(instr[5]), .arg0(i12), .arg1(rs2v[4:0]), .mux_out(mux_2x5_1_mux_out));
  and and_4 (load_store, instr[0], instr[1], ~instr[2], ~instr[3], ~instr[4], ~instr[6]);  // AND_Gate
  mux_2x32 mux_2x32_1 (.index(instr_write), .arg0(load_store_pointer), .arg1(pc), .mux_out(pointer));
  mux_2x32 mux_2x32_2 (.index(manual_instr_write), .arg0(ram_word), .arg1(manual_instr), .mux_out(instr_data));
  // Probe on reg_data
  assign xor_1_out = bit_extender_3_out ^ B;  // XOR_Gate xor_1, 32 bits wide
  lshift lshift_2 (.val({{24{1'b0}}, rs2v[7:0]}), .shamt({pointer[1:0], 3'b000}), .shifted(lshift_2_shifted));
  lshift lshift_3 (.val(32'hff), .shamt({pointer[1:0], 3'b000}), .shifted(lshift_3_shifted));
  lshift lshift_4 (.val({{16{1'b0}}, rs2v[15:0]}), .shamt({pointer[1], 4'b0000}), .shifted(lshift_4_shifted));
  lshift lshift_5 (.val(32'hffff), .shamt({pointer[1], 4'b0000}), .shifted(lshift_5_shifted));
  and and_5 (and_5_out, ~funct3[2], ram_byte[7]);  // AND_Gate
  and and_6 (and_6_out, ~funct3[2], ram_halfword[15]);  // AND_Gate
  assign and_7_out = ram_word & ~lshift_3_shifted;  // AND_Gate and_7, 32 bits wide
  assign and_8_out = ram_word & ~lshift_5_shifted;  // AND_Gate and_8, 32 bits wide
  nc_adder_32 nc_adder_32_3 (.A({funct7, i12, i20, funct3, {12{1'b0}}}), .B(pc), .sum(nc_adder_32_3_sum));
  assign bit_extender_4_out = {{24{and_5_out}}, ram_byte};  // Bit_Extender bit_extender_4
  assign bit_extender_5_out = {{16{and_6_out}}, ram_halfword};  // Bit_Extender bit_extender_5
  mux_2x32 mux_2x32_10 (.index(instr[5]), .arg0(i12_32), .arg1(i5_7_32), .mux_out(mux_2x32_10_mux_out));
  assign or_4_out = lshift_2_shifted | and_7_out;  // OR_Gate or_4, 32 bits wide
  assign or_5_out = lshift_4_shifted | and_8_out;  // OR_Gate or_5, 32 bits wide
  mux_2x32 mux_2x32_3 (.index(instr[5]), .arg0(i12_32), .arg1(rs2v), .mux_out(B));
  adder_32 adder_32_1 (
    .carry_in(and_3_out), .A(A), .B(xor_1_out), .sum(adder_32_1_sum), .carry_out(adder_32_1_carry_out));
  // NoConnect on adder_32_1_carry_out
  lshift lshift_1 (.val(A), .shamt(mux_2x5_1_mux_out), .shifted(lshift_1_shifted));
  rshift rshift_1 (.val(A), .shamt(mux_2x5_1_mux_out), .arith(funct7[5]), .shifted(rshift_1_shifted));
  comparator_32 comparator_32_1 (
    .A(A), .B(B), .eq(comparator_32_1_eq), .lts(comparator_32_1_lts), .ltu(comparator_32_1_ltu));  // open: gts, gtu
  assign xor_2_out = A ^ B;  // XOR_Gate xor_2, 32 bits wide
  assign or_6_out = A | B;  // OR_Gate or_6, 32 bits wide
  assign and_9_out = A & B;  // AND_Gate and_9, 32 bits wide
  and and_10 (and_10_out, instr[0], instr[1], instr[2], ~instr[3], instr[4], ~instr[6]);  // AND_Gate
  assign bit_extender_6_out = {{31{1'b0}}, comparator_32_1_lts};  // Bit_Extender bit_extender_6
  assign bit_extender_7_out = {{31{1'b0}}, comparator_32_1_ltu};  // Bit_Extender bit_extender_7
  and and_11 (and_11_out, ~instr[5], load_store);  // AND_Gate
  assign bit_extender_8_out = {{31{load_store}}, load_store};  // Bit_Extender bit_extender_8
  nc_adder_32 nc_adder_32_4 (.A(A), .B(mux_2x32_10_mux_out), .sum(nc_adder_32_4_sum));
  and and_12 (and_12_out, instr[5], load_store);
  nand nand_1 (nand_1_out, instr[0], instr[1], ~instr[2], ~instr[3], instr[5]);  // NAND_Gate
  and and_13 (and_13_out, instr[4], ~instr[6]);  // AND_Gate
  assign bit_extender_9_out = {{31{and_10_out}}, and_10_out};  // Bit_Extender bit_extender_9
  assign ui_reg_data = bit_extender_9_out & mux_2x32_9_mux_out;  // AND_Gate and_14, 32 bits wide
  mux_2x32 mux_2x32_9 (
    .index(instr[5]), .arg0(nc_adder_32_3_sum), .arg1({funct7, i12, i20, funct3, {12{1'b0}}}),
    .mux_out(mux_2x32_9_mux_out));
  assign bit_extender_10_out = {{31{and_11_out}}, and_11_out};  // Bit_Extender bit_extender_10
  assign load_reg_data = bit_extender_10_out & mux_4x32_1_mux_out;  // AND_Gate and_15, 32 bits wide
  mux_4x32 mux_4x32_1 (
    .index(funct3[1:0]), .arg0(bit_extender_4_out), .arg1(bit_extender_5_out), .arg2(ram_word),
    .arg3({32{1'b0}}), .mux_out(mux_4x32_1_mux_out));
  assign load_store_pointer = bit_extender_8_out & nc_adder_32_4_sum;  // AND_Gate and_16, 32 bits wide
  assign bit_extender_11_out = {{31{and_12_out}}, and_12_out};  // Bit_Extender bit_extender_11
  assign ram_data = bit_extender_11_out & mux_4x32_2_mux_out;  // AND_Gate and_17, 32 bits wide
  mux_4x32 mux_4x32_2 (
    .index(funct3[1:0]), .arg0(or_4_out), .arg1(or_5_out), .arg2(rs2v), .arg3({32{1'b0}}),
    .mux_out(mux_4x32_2_mux_out));
  or or_7 (reg_write, nand_1_out, and_13_out);
  assign reg_data = ui_reg_data | alu_reg_data | load_reg_data | jump_reg_data;  // OR_Gate or_8, 32 bits wide
  and and_18 (and_18_out, instr[0], instr[1], ~instr[2], ~instr[3], instr[4], ~instr[6]);  // AND_Gate
  mux_8x32 mux_8x32_1 (
    .index(funct3), .arg0(adder_32_1_sum), .arg1(lshift_1_shifted), .arg2(bit_extender_6_out),
    .arg3(bit_extender_7_out), .arg4(xor_2_out), .arg5(rshift_1_shifted), .arg6(or_6_out), .arg7(and_9_out),
    .mux_out(mux_8x32_1_mux_out));
  assign bit_extender_12_out = {{31{and_18_out}}, and_18_out};  // Bit_Extender bit_extender_12
  assign alu_reg_data = bit_extender_12_out & mux_8x32_1_mux_out;  // AND_Gate and_19, 32 bits wide
  mux_4x1 mux_4x1_1 (
    .index(funct3[2:1]), .arg0(comparator_32_1_eq), .arg1(1'b0), .arg2(comparator_32_1_lts),
    .arg3(comparator_32_1_ltu), .mux_out(mux_4x1_1_mux_out));
  and and_20 (and_20_out, jump, xor_3_out);
  xor xor_3 (xor_3_out, funct3[0], mux_4x1_1_mux_out);
  and and_21 (jump, instr[0], instr[1], ~instr[4], instr[5], instr[6]);  // AND_Gate
  assign bit_extender_13_out = {{31{and_22_out}}, and_22_out};  // Bit_Extender bit_extender_13
  and and_22 (and_22_out, jump, instr[2]);
  and and_23 (and_23_out, instr[2], jump, ~instr[3]);  // AND_Gate
  and and_24 (and_24_out, instr[2], jump);
  mux_2x32 mux_2x32_8 (.index(and_20_out), .arg0(32'h4), .arg1(i5_7_32), .mux_out(mux_2x32_8_mux_out));
  assign bit_extender_14_out = {{12{funct7[6]}}, {funct7, i12, i20, funct3}};  // Bit_Extender bit_extender_14
  assign jump_reg_data = next_pc & bit_extender_13_out;  // AND_Gate and_25, 32 bits wide
  mux_2x32 mux_2x32_7 (
    .index(and_24_out), .arg0(mux_2x32_8_mux_out), .arg1(bit_extender_14_out), .mux_out(mux_2x32_7_mux_out));
  nc_adder_32 nc_adder_32_1 (.A(pc), .B(32'h4), .sum(next_pc));
  mux_2x32 mux_2x32_5 (.index(and_23_out), .arg0(pc), .arg1(A), .mux_out(mux_2x32_5_mux_out));
  mux_2x32 mux_2x32_6 (.index(and_23_out), .arg0(mux_2x32_7_mux_out), .arg1(i12_32), .mux_out(mux_2x32_6_mux_out));
  nc_adder_32 nc_adder_32_2 (.A(mux_2x32_5_mux_out), .B(mux_2x32_6_mux_out), .sum(nc_adder_32_2_sum));
  mux_2x32 mux_2x32_4 (.index(manual_pc_write), .arg0(nc_adder_32_2_sum), .arg1(manual_pc), .mux_out(pc_data));

  // Other names for the same wires on the sheet: i20 (some bits) = {funct7, i12, funct3};
  //   instr[31:7] = {funct7, i12, i20, funct3, i5}; rs1[4:0] = i20; rs2[4:0] = i12; i7[6:0] = funct7;
  //   i12[11:5] = funct7; op[6:0] = instr; nimm = instr[5]; ram_write = instr[5]; store = instr[5]; rd[4:0] = i5;
  //   rs1v[31:0] = A; store_ram_data[31:0] = ram_data
endmodule

module seven_segment (
  input  [3:0] hex_digit,
  output [7:0] display_out
);

  mux_16x8 mux_16x8_1 (
    .index(hex_digit), .arg0(8'hc0), .arg1(8'hf9), .arg2(8'ha4), .arg3(8'hb0), .arg4(8'h99), .arg5(8'h92),
    .arg6(8'h82), .arg7(8'hf8), .arg8(8'h80), .arg9(8'h90), .arg10(8'h88), .arg11(8'h83), .arg12(8'hc6),
    .arg13(8'ha1), .arg14(8'h86), .arg15(8'h8e), .mux_out(display_out));
endmodule

module shift_word (
  input  [7:0] byte_in,
  input  shift,
  output [31:0] word_out
);

  Register register_1 (.D(byte_in), .en(1'b1), .clk(shift), .Q(word_out[7:0]));  // open: clr
  Register register_2 (.D(word_out[7:0]), .en(1'b1), .clk(shift), .Q(word_out[15:8]));  // open: clr
  Register register_3 (.D(word_out[15:8]), .en(1'b1), .clk(shift), .Q(word_out[23:16]));  // open: clr
  Register register_4 (.D(word_out[23:16]), .en(1'b1), .clk(shift), .Q(word_out[31:24]));  // open: clr
endmodule

module debouncer (
  input  data_in,
  input  clock,
  output debounced
);

  wire comparator_1_eq, not_1_out, xor_1_out;
  wire [19:0] counter_1_q;

  xor xor_1 (xor_1_out, debounced, data_in);
  Counter #(.max('hfffff), .ongoal("stay"), .width(20)) counter_1 (
    .clr(not_1_out), .up(1'b1), .count(xor_1_out), .clk(clock), .Q(counter_1_q));  // open: load, D, carry
  not not_1 (not_1_out, xor_1_out);
  T_Flip_Flop t_ff_1 (.T(1'b1), .clk(comparator_1_eq), .Q(debounced));  // open: Qn, reset, preset
  Comparator #(.mode("unsigned"), .width(20)) comparator_1 (
    .a(counter_1_q), .b(20'h14), .eq(comparator_1_eq));  // open: gt, lt
endmodule

module de10_interface (
  input  sw0,
  input  sw1,
  input  sw2,
  input  sw3,
  input  sw4,
  input  sw5,
  input  sw6,
  input  sw7,
  input  sw8,
  input  sw9,
  input  btn0,
  input  btn1,
  output led0,
  output led1,
  output led2,
  output led3,
  output led4,
  output led5,
  output led6,
  output led7,
  output [7:0] disp0,
  output [7:0] disp1,
  output [7:0] disp2,
  output [7:0] disp3,
  output [7:0] disp4,
  output [7:0] disp5
);

  wire and_1_out, and_3_out, and_4_out, and_5_out, btn0_t, btn1_t, clock_1_out, manual_exec,
       manual_instr_write, manual_pc_write, not_1_out, not_2_out, reset, tick;
  wire [31:0] a0, input_word;
  wire [31:8] display_word;

  not not_1 (not_1_out, btn0);
  not not_2 (not_2_out, btn1);
  Clock clock_1 (.out(clock_1_out));
  and and_1 (and_1_out, ~sw8, ~sw9);  // AND_Gate
  and and_2 (manual_pc_write, and_1_out, btn0_t);
  and and_3 (and_3_out, and_1_out, btn1_t);
  debouncer debouncer_1 (.data_in(not_1_out), .clock(clock_1_out), .debounced(btn0_t));
  debouncer debouncer_2 (.data_in(not_2_out), .clock(clock_1_out), .debounced(btn1_t));
  shift_word shift_word_1 (
    .byte_in({sw7, sw6, sw5, sw4, sw3, sw2, sw1, sw0}), .shift(and_3_out), .word_out(input_word));
  and and_4 (and_4_out, sw8, ~sw9);  // AND_Gate
  // Probe on a0
  cpu cpu_1 (
    .manual_exec(manual_exec), .manual_instr(input_word), .manual_instr_write(manual_instr_write),
    .manual_pc(input_word), .manual_pc_write(manual_pc_write), .reset(reset), .clock(tick), .a0(a0));
  and and_5 (and_5_out, sw8, sw9);
  and and_6 (reset, and_5_out, btn0_t);
  and and_7 (tick, and_5_out, btn1_t);
  and and_8 (manual_exec, and_4_out, btn0_t);
  and and_9 (manual_instr_write, and_4_out, btn1_t);
  mux_2x32 mux_2x32_1 (
    .index(and_5_out), .arg0(input_word), .arg1(a0),
    .mux_out({display_word, led7, led6, led5, led4, led3, led2, led1, led0}));
  seven_segment seven_segment_1 (.hex_digit(display_word[11:8]), .display_out(disp0));
  seven_segment seven_segment_2 (.hex_digit(display_word[15:12]), .display_out(disp1));
  seven_segment seven_segment_3 (.hex_digit(display_word[19:16]), .display_out(disp2));
  seven_segment seven_segment_4 (.hex_digit(display_word[23:20]), .display_out(disp3));
  seven_segment seven_segment_5 (.hex_digit(display_word[27:24]), .display_out(disp4));
  seven_segment seven_segment_6 (.hex_digit(display_word[31:28]), .display_out(disp5));

  // Other names for the same wires on the sheet: display_word[7:0] = {led7, led6, led5, led4, led3, led2, led1, led0};
  //   manual_instr[31:0] = input_word; manual_pc[31:0] = input_word

  // Notes on the sheet:
  //   btn0: initial=0x1
  //   btn1: initial=0x1
endmodule
